// Logisim project 8bitProgrammableComputer.circ as structural Verilog: 3 circuits, main circuit main
module main (
);

  wire clock_1_out, RST_out;
  wire [3:0] alu_1_aluout, alu_1_aluout_2, counter4_1_cnt;
  wire [19:0] rom_1_data;

  Clock clock_1 (.out(clock_1_out));
  Button RST (.out(RST_out));
  Counter4 counter4_1 (.CNT(counter4_1_cnt), .R(RST_out), .clk(clock_1_out));
  ROM #(.addrWidth(4), .dataWidth(20)) rom_1 (.addr(counter4_1_cnt), .data(rom_1_data));
  Hex_Digit_Display hex_digit_display_1 (.value(alu_1_aluout_2));  // open: dp
  ALU alu_1 (
    .S1(rom_1_data[17]), .S0(rom_1_data[16]), .A(rom_1_data[15:8]), .B(rom_1_data[7:0]), .An(rom_1_data[19]),
    .Bn(rom_1_data[18]), .ALUOut({alu_1_aluout_2, alu_1_aluout}));  // open: Cin
  Hex_Digit_Display hex_digit_display_2 (.value(alu_1_aluout));  // open: dp

  // Notes on the sheet:
  //   contents of rom_1 (hex, n*v repeats v):
  //   20809 60f02 c0101
endmodule

module ALU (
  input  Bn,
  input  An,
  input  Cin,
  input  [7:0] A,
  input  [7:0] B,
  input  S0,
  input  S1,
  output [7:0] ALUOut
);

  wire or_2_out;
  wire [7:0] adder_1_out, and_1_out, multiplexer_1_out, multiplexer_2_out, not_1_out, not_2_out, or_1_out;

  assign not_1_out = ~A;  // NOT_Gate not_1, 8 bits wide
  assign not_2_out = ~B;  // NOT_Gate not_2, 8 bits wide
  Multiplexer #(.width(8), .enable("false")) multiplexer_1 (
    .in0(A), .in1(not_1_out), .out(multiplexer_1_out), .sel(An));
  Multiplexer #(.width(8), .enable("false")) multiplexer_2 (
    .in0(B), .in1(not_2_out), .out(multiplexer_2_out), .sel(Bn));
  assign and_1_out = multiplexer_1_out & multiplexer_2_out;  // AND_Gate and_1, 8 bits wide
  assign or_1_out = multiplexer_1_out | multiplexer_2_out;  // OR_Gate or_1, 8 bits wide
  or or_2 (or_2_out, Bn, An, Cin);
  Adder adder_1 (.a(multiplexer_1_out), .b(multiplexer_2_out), .out(adder_1_out), .cin(or_2_out));  // open: cout
  Multiplexer #(.select(2), .width(8), .enable("false")) multiplexer_3 (
    .in0(and_1_out), .in1(or_1_out), .in2(adder_1_out), .out(ALUOut), .sel({S1, S0}));  // open: in3
endmodule

module Counter4 (
  input  clk,
  input  R,
  output [3:0] CNT
);

  wire d_ff_1_qn, d_ff_2_qn, d_ff_3_qn, d_ff_4_qn;

  D_Flip_Flop d_ff_1 (.D(d_ff_1_qn), .clk(clk), .Q(CNT[0]), .Qn(d_ff_1_qn), .reset(R));  // open: preset
  D_Flip_Flop d_ff_2 (.D(d_ff_2_qn), .clk(d_ff_1_qn), .Q(CNT[1]), .Qn(d_ff_2_qn), .reset(R));  // open: preset
  D_Flip_Flop d_ff_3 (.D(d_ff_3_qn), .clk(d_ff_2_qn), .Q(CNT[2]), .Qn(d_ff_3_qn), .reset(R));  // open: preset
  D_Flip_Flop d_ff_4 (.D(d_ff_4_qn), .clk(d_ff_3_qn), .Q(CNT[3]), .Qn(d_ff_4_qn), .reset(R));  // open: preset
endmodule
